// Logisim project 4 bit comparator.circ as structural Verilog: 1 circuit, main circuit main
module main (
  input  [3:0] A,
  input  [3:0] B
);

  wire comparator_1_eq, comparator_1_gt, comparator_1_lt;

  DotMatrix #(.inputtype("row"), .matrixcols(1), .matrixrows(3)) dotmatrix_1 (
    .row0(comparator_1_gt), .row1(comparator_1_eq), .row2(comparator_1_lt));
  Comparator #(.width(4), .mode("unsigned")) comparator_1 (
    .a(A), .b(B), .gt(comparator_1_gt), .eq(comparator_1_eq), .lt(comparator_1_lt));

  // Notes on the sheet:
  //   A>B
  //   A=B
  //   A<B
endmodule
