// Logisim project 6 Gates.circ as structural Verilog: 1 circuit, main circuit main
module main (
  input  A,
  input  A_2,
  input  B,
  input  B_2,
  input  B_3,
  input  A_3,
  input  B_4,
  input  B_5,
  input  A_4,
  input  A_5,
  input  B_6,
  output Y,
  output Y_2,
  output Y_3,
  output Y_4,
  output Y_5,
  output Y_6
);

  and and_1 (Y, A, B);
  nand nand_1 (Y_3, B_3, B_4);
  not not_1 (Y_5, A_5);
  or or_1 (Y_2, A_2, B_2);
  nor nor_1 (Y_4, A_3, B_5);
  xor xor_1 (Y_6, A_4, B_6);

  // Notes on the sheet:
  //   AND
  //   NAND
  //   OR
  //   NOR
  //   XOR
endmodule
