// Logisim project Full Adder & Subtractor.circ as structural Verilog: 1 circuit, main circuit main
module main (
  input  A,
  input  B,
  input  Cin,
  input  A_2,
  input  B_2,
  input  Bin,
  output SUM,
  output CARRY,
  output Difference,
  output Bout
);

  wire and_1_out, and_2_out, and_3_out, and_4_out, not_1_out, xor_1_out, xor_2_out;

  and and_1 (and_1_out, B, Cin);
  and and_2 (and_2_out, B_2, Bin);
  xor xor_1 (xor_1_out, B, Cin);
  xor xor_2 (xor_2_out, B_2, Bin);
  not not_1 (not_1_out, A_2);
  xor xor_3 (SUM, A, xor_1_out);
  and and_3 (and_3_out, A, xor_1_out);
  xor xor_4 (Difference, A_2, xor_2_out);
  and and_4 (and_4_out, not_1_out, xor_2_out);
  or or_1 (CARRY, and_3_out, and_1_out);
  or or_2 (Bout, and_4_out, and_2_out);

  // Notes on the sheet:
  //   FULL ADDER
  //   FULL SUBTRACTOR
endmodule
