// Logisim project PS.circ as structural Verilog: 1 circuit, main circuit main
module main (
  input  A,
  input  B,
  input  C,
  input  D,
  output out_5
);

  wire and_1_out, and_2_out, and_3_out, and_4_out;

  and and_1 (and_1_out, ~A, ~B);  // AND_Gate
  and and_2 (and_2_out, ~and_1_out, ~D);  // AND_Gate
  and and_3 (and_3_out, ~B, ~C);  // AND_Gate
  and and_4 (and_4_out, and_3_out, D);
  or or_1 (out_5, and_2_out, and_4_out);

  // Notes on the sheet:
  //   8
  //   4
  //   2
  //   1
  //   OUTPUT
endmodule
