// Logisim project Prime Number detector.circ as structural Verilog: 1 circuit, main circuit main
module main (
  input  A,
  input  B,
  input  C,
  input  D,
  output F
);

  wire and_1_out, and_2_out, and_3_out;

  and and_1 (and_1_out, A, ~B, C);  // AND_Gate
  and and_2 (and_2_out, A, C, ~D);  // AND_Gate
  and and_3 (and_3_out, A, ~C, B);  // AND_Gate
  or or_1 (F, and_1_out, and_2_out, and_3_out);

  // Notes on the sheet:
  //   1
  //   2
  //   4
  //   8
endmodule
