// Logisim project 1.circ as structural Verilog: 1 circuit, main circuit main
module main (
  input  in_1
);

  // OR_Gate or_1 is placed but not wired
  // OR_Gate or_2 is placed but not wired
  // OR_Gate or_3 is placed but not wired
endmodule
