// Logisim project OR using NOR.circ as structural Verilog: 1 circuit, main circuit main
module main (
  input  A,
  input  B,
  output Y
);

  wire xnor_1_out;

  xnor xnor_1 (xnor_1_out, A, B);
  not not_1 (Y, xnor_1_out);
endmodule
