// Logisim project XOR using NOR.circ as structural Verilog: 1 circuit, main circuit main
module main (
  input  A,
  input  B,
  output Y
);

  wire nor_1_out, nor_2_out, nor_3_out;

  nor nor_1 (nor_1_out, A, B);
  nor nor_2 (nor_2_out, A, nor_1_out);
  nor nor_3 (nor_3_out, nor_1_out, B);
  nor nor_4 (Y, nor_2_out, nor_3_out);

  // Notes on the sheet:
  //   X-NOR
  //   (A+B)'
  //   (B+(A+B)')'
  //   (A+(A+B)')'
  //   A.B
endmodule
